// Logisim project mips_circuit.circ as structural Verilog: 3 circuits, main circuit main
module main (
  input  [31:0] Zero_Value,
  input  [31:0] t0_IN,
  input  lw_t0,
  input  [31:0] t1_IN,
  input  lw_t1,
  input  [31:0] t2_IN,
  input  lw_t2,
  input  [31:0] t3_IN,
  input  lw_t3,
  input  [31:0] t4_IN,
  input  lw_t4,
  input  [31:0] t5_IN,
  input  lw_t5,
  input  [31:0] t6_IN,
  input  lw_t6,
  input  [31:0] t7_IN,
  input  lw_t7,
  input  ALU3,
  input  [31:0] Instruction,
  output Jump,
  output ResDst,
  output ALUSrc,
  output MemToReg,
  output WriteReg,
  output ReadMem,
  output WriteMem,
  output [31:0] Result,
  output Branch,
  output opALU0,
  output opALU1,
  output Zero_Flag,
  output Overflow,
  output Underflow,
  output ALU2,
  output ALU1,
  output ALU0
);

  wire addi_out, and_2_out, and_3_out, clock_signal_out, or_3_out;
  wire [4:0] multiplexer_1_out;
  wire [31:0] adder_1_out, and_4_out, not_1_out, or_6_out, Registers_read_register_1,
       Registers_read_register_2, subtractor_1_out;

  and R (opALU1, ~Instruction[26], ~Instruction[27], ~Instruction[28], ~Instruction[29], ~Instruction[30], ~Instruction[31]);  // AND_Gate
  Multiplexer #(.width(5)) multiplexer_1 (
    .in0(Instruction[20:16]), .in1(Instruction[15:11]), .out(multiplexer_1_out), .sel(opALU1));
  and lw (MemToReg, Instruction[26], Instruction[27], ~Instruction[28], ~Instruction[29], ~Instruction[30], Instruction[31]);  // AND_Gate
  and sw (WriteMem, Instruction[26], Instruction[27], ~Instruction[28], Instruction[29], ~Instruction[30], Instruction[31]);  // AND_Gate
  and beq (Branch, ~Instruction[26], ~Instruction[27], Instruction[28], ~Instruction[29], ~Instruction[30], ~Instruction[31]);  // AND_Gate
  and addi (addi_out, ~Instruction[26], ~Instruction[27], ~Instruction[28], Instruction[29], ~Instruction[30], ~Instruction[31]);  // AND_Gate
  and J (Jump, ~Instruction[26], Instruction[27], ~Instruction[28], ~Instruction[29], ~Instruction[30], ~Instruction[31]);  // AND_Gate
  or or_1 (ALUSrc, MemToReg, addi_out, WriteMem);
  or or_2 (WriteReg, opALU1, addi_out, MemToReg);
  or or_3 (or_3_out, Instruction[3], Instruction[0]);
  and and_1 (ALU0, opALU1, or_3_out);
  and and_2 (and_2_out, opALU1, Instruction[1]);
  and and_3 (and_3_out, ~Branch, opALU1);  // AND_Gate
  or or_4 (ALU2, Branch, and_2_out);
  or or_5 (ALU1, ~opALU1, ~Instruction[2]);  // OR_Gate
  Clock clock_signal (.out(clock_signal_out));
  Register_File Registers (
    .ALU_Result(Result), .Zero_Value(Zero_Value), .t0_IN(t0_IN), .lw_t0(lw_t0), .t1_IN(t1_IN), .lw_t1(lw_t1),
    .t2_IN(t2_IN), .lw_t2(lw_t2), .t3_IN(t3_IN), .lw_t3(lw_t3), .t4_IN(t4_IN), .lw_t4(lw_t4), .t5_IN(t5_IN),
    .lw_t5(lw_t5), .t6_IN(t6_IN), .lw_t6(lw_t6), .t7_IN(t7_IN), .lw_t7(lw_t7),
    .Clock_Signal(clock_signal_out), .RD(multiplexer_1_out), .RS_IN(Instruction[25:21]),
    .RT_IN(Instruction[20:16]), .RegWrite(WriteReg), .Read_Register_1(Registers_read_register_1),
    .Read_Register_2(Registers_read_register_2));
  assign and_4_out = Registers_read_register_1 & Registers_read_register_2;  // AND_Gate and_4, 32 bits wide
  assign or_6_out = Registers_read_register_1 | Registers_read_register_2;  // OR_Gate or_6, 32 bits wide
  Adder #(.width(32)) adder_1 (
    .a(Registers_read_register_1), .b(Registers_read_register_2), .out(adder_1_out), .cout(Overflow));  // open: cin
  Subtractor #(.width(32)) subtractor_1 (
    .a(Registers_read_register_1), .b(Registers_read_register_2), .out(subtractor_1_out), .bout(Underflow));  // open: bin
  Multiplexer #(.enable("true"), .select(4), .width(32)) multiplexer_2 (
    .in0(and_4_out), .in1(or_6_out), .in2(adder_1_out), .in6(subtractor_1_out), .out(Result),
    .sel({ALU3, ALU2, ALU1, ALU0}), .en(and_3_out));  // open: in3, in4, in5, in7, in8, in9, in10, in11, in12, in13, in14, in15
  assign not_1_out = ~Result;  // NOT_Gate not_1, 32 bits wide
  and and_5 (Zero_Flag, not_1_out[0], not_1_out[1], not_1_out[2], not_1_out[3], not_1_out[4], not_1_out[5], not_1_out[6], not_1_out[7], not_1_out[8], not_1_out[9], not_1_out[10], not_1_out[11], not_1_out[12], not_1_out[13], not_1_out[14], not_1_out[15], not_1_out[17], not_1_out[18], not_1_out[19], not_1_out[20], not_1_out[21], not_1_out[22], not_1_out[23], not_1_out[24], not_1_out[25], not_1_out[26], not_1_out[27], not_1_out[28], not_1_out[29], not_1_out[30], not_1_out[31], not_1_out[16]);

  assign opALU0 = Branch;
  assign ReadMem = MemToReg;
  assign ResDst = opALU1;

  // Notes on the sheet:
  //   OP code
  //   RS
  //   RT
  //   RD
  //   Shamt
  //   Bit 5
  //   Bit 4
  //   Bit 3
  //   Bit 2
  //   Bit 1
  //   Bit 0
  //   Funct
  //   RegDst  
  //   Control Signal
  //   ALU Control
  //   Bit 5
  //   Bit 4
  //   Bit 3
  //   Bit 2
  //   Bit 1
  //   Bit 0
  //   Read Register 1
  //   Read Register 2
  //   AND
  //   OR
  //   ADD
  //   SUB
  //   ALU
endmodule

module Register_File (
  input  [31:0] ALU_Result,
  input  [31:0] Zero_Value,
  input  [31:0] t0_IN,
  input  lw_t0,
  input  [31:0] t1_IN,
  input  lw_t1,
  input  [31:0] t2_IN,
  input  lw_t2,
  input  [31:0] t3_IN,
  input  lw_t3,
  input  [31:0] t4_IN,
  input  lw_t4,
  input  [31:0] t5_IN,
  input  lw_t5,
  input  [31:0] t6_IN,
  input  lw_t6,
  input  [31:0] t7_IN,
  input  lw_t7,
  input  Clock_Signal,
  input  [4:0] RD,
  input  [4:0] RS_IN,
  input  [4:0] RT_IN,
  input  RegWrite,
  output [31:0] Read_Register_1,
  output [31:0] Read_Register_2
);

  wire demultiplexer_2_out1, demultiplexer_2_out2, demultiplexer_2_out3, demultiplexer_2_out4,
       demultiplexer_2_out5, demultiplexer_2_out6, demultiplexer_2_out7, demultiplexer_2_out8,
       demultiplexer_2_out9, demultiplexer_2_out10, demultiplexer_2_out11, demultiplexer_2_out12,
       demultiplexer_2_out13, demultiplexer_2_out14, demultiplexer_2_out15, demultiplexer_2_out16,
       demultiplexer_2_out17, demultiplexer_2_out18, demultiplexer_2_out19, demultiplexer_2_out20,
       demultiplexer_2_out21, demultiplexer_2_out22, demultiplexer_2_out23, demultiplexer_2_out24,
       demultiplexer_2_out25, demultiplexer_2_out26, demultiplexer_2_out27, demultiplexer_2_out28,
       demultiplexer_2_out29, demultiplexer_2_out30, demultiplexer_2_out31, load_t0_enable, load_t1_enable,
       load_t2_enable, load_t3_enable, load_t4_enable, load_t5_enable, load_t6_enable, load_t7_enable;
  wire [31:0] a0_q, a1_q, a2_q, a3_q, at_q, demultiplexer_1_out1, demultiplexer_1_out2, demultiplexer_1_out3,
       demultiplexer_1_out4, demultiplexer_1_out5, demultiplexer_1_out6, demultiplexer_1_out7,
       demultiplexer_1_out8, demultiplexer_1_out9, demultiplexer_1_out10, demultiplexer_1_out11,
       demultiplexer_1_out12, demultiplexer_1_out13, demultiplexer_1_out14, demultiplexer_1_out15,
       demultiplexer_1_out16, demultiplexer_1_out17, demultiplexer_1_out18, demultiplexer_1_out19,
       demultiplexer_1_out20, demultiplexer_1_out21, demultiplexer_1_out22, demultiplexer_1_out23,
       demultiplexer_1_out24, demultiplexer_1_out25, demultiplexer_1_out26, demultiplexer_1_out27,
       demultiplexer_1_out28, demultiplexer_1_out29, demultiplexer_1_out30, demultiplexer_1_out31, fp_q,
       gp_q, k0_q, k1_q, load_t0_write, load_t1_write, load_t2_write, load_t3_write, load_t4_write,
       load_t5_write, load_t6_write, load_t7_write, ra_q, s0_q, s1_q, s2_q, s3_q, s4_q, s5_q, s6_q, s7_q,
       sp_q, t0_q, t1_q, t2_q, t3_q, t4_q, t5_q, t6_q, t7_q, t8_q, t9_q, v0_q, v1_q, zero_q;

  Demultiplexer #(.select(5), .width(32)) demultiplexer_1 (
    .out1(demultiplexer_1_out1), .out2(demultiplexer_1_out2), .out3(demultiplexer_1_out3),
    .out4(demultiplexer_1_out4), .out5(demultiplexer_1_out5), .out6(demultiplexer_1_out6),
    .out7(demultiplexer_1_out7), .out8(demultiplexer_1_out8), .out9(demultiplexer_1_out9),
    .out10(demultiplexer_1_out10), .out11(demultiplexer_1_out11), .out12(demultiplexer_1_out12),
    .out13(demultiplexer_1_out13), .out14(demultiplexer_1_out14), .out15(demultiplexer_1_out15),
    .out16(demultiplexer_1_out16), .out17(demultiplexer_1_out17), .out18(demultiplexer_1_out18),
    .out19(demultiplexer_1_out19), .out20(demultiplexer_1_out20), .out21(demultiplexer_1_out21),
    .out22(demultiplexer_1_out22), .out23(demultiplexer_1_out23), .out24(demultiplexer_1_out24),
    .out25(demultiplexer_1_out25), .out26(demultiplexer_1_out26), .out27(demultiplexer_1_out27),
    .out28(demultiplexer_1_out28), .out29(demultiplexer_1_out29), .out30(demultiplexer_1_out30),
    .out31(demultiplexer_1_out31), .in(ALU_Result), .sel(RD));  // open: out0
  Demultiplexer #(.select(5)) demultiplexer_2 (
    .out1(demultiplexer_2_out1), .out2(demultiplexer_2_out2), .out3(demultiplexer_2_out3),
    .out4(demultiplexer_2_out4), .out5(demultiplexer_2_out5), .out6(demultiplexer_2_out6),
    .out7(demultiplexer_2_out7), .out8(demultiplexer_2_out8), .out9(demultiplexer_2_out9),
    .out10(demultiplexer_2_out10), .out11(demultiplexer_2_out11), .out12(demultiplexer_2_out12),
    .out13(demultiplexer_2_out13), .out14(demultiplexer_2_out14), .out15(demultiplexer_2_out15),
    .out16(demultiplexer_2_out16), .out17(demultiplexer_2_out17), .out18(demultiplexer_2_out18),
    .out19(demultiplexer_2_out19), .out20(demultiplexer_2_out20), .out21(demultiplexer_2_out21),
    .out22(demultiplexer_2_out22), .out23(demultiplexer_2_out23), .out24(demultiplexer_2_out24),
    .out25(demultiplexer_2_out25), .out26(demultiplexer_2_out26), .out27(demultiplexer_2_out27),
    .out28(demultiplexer_2_out28), .out29(demultiplexer_2_out29), .out30(demultiplexer_2_out30),
    .out31(demultiplexer_2_out31), .in(RegWrite), .sel(RD));  // open: out0
  load load_t0 (
    .ALU(demultiplexer_1_out8), .Load_IN(t0_IN), .Slection_Bit(lw_t0), .RegWrite(demultiplexer_2_out8),
    .Write(load_t0_write), .Enable(load_t0_enable));
  load load_t1 (
    .ALU(demultiplexer_1_out9), .Load_IN(t1_IN), .Slection_Bit(lw_t1), .RegWrite(demultiplexer_2_out9),
    .Write(load_t1_write), .Enable(load_t1_enable));
  load load_t2 (
    .ALU(demultiplexer_1_out10), .Load_IN(t2_IN), .Slection_Bit(lw_t2), .RegWrite(demultiplexer_2_out10),
    .Write(load_t2_write), .Enable(load_t2_enable));
  load load_t3 (
    .ALU(demultiplexer_1_out11), .Load_IN(t3_IN), .Slection_Bit(lw_t3), .RegWrite(demultiplexer_2_out11),
    .Write(load_t3_write), .Enable(load_t3_enable));
  load load_t4 (
    .ALU(demultiplexer_1_out12), .Load_IN(t4_IN), .Slection_Bit(lw_t4), .RegWrite(demultiplexer_2_out12),
    .Write(load_t4_write), .Enable(load_t4_enable));
  load load_t5 (
    .ALU(demultiplexer_1_out13), .Load_IN(t5_IN), .Slection_Bit(lw_t5), .RegWrite(demultiplexer_2_out13),
    .Write(load_t5_write), .Enable(load_t5_enable));
  load load_t6 (
    .ALU(demultiplexer_1_out14), .Load_IN(t6_IN), .Slection_Bit(lw_t6), .RegWrite(demultiplexer_2_out14),
    .Write(load_t6_write), .Enable(load_t6_enable));
  load load_t7 (
    .ALU(demultiplexer_1_out15), .Load_IN(t7_IN), .Slection_Bit(lw_t7), .RegWrite(demultiplexer_2_out15),
    .Write(load_t7_write), .Enable(load_t7_enable));
  Register #(.width(32)) zero (.D(Zero_Value), .en(Clock_Signal), .clk(Clock_Signal), .Q(zero_q));  // open: clr
  Register #(.width(32)) at (
    .D(demultiplexer_1_out1), .en(demultiplexer_2_out1), .clk(Clock_Signal), .Q(at_q));  // open: clr
  Register #(.width(32)) v0 (
    .D(demultiplexer_1_out2), .en(demultiplexer_2_out2), .clk(Clock_Signal), .Q(v0_q));  // open: clr
  Register #(.width(32)) v1 (
    .D(demultiplexer_1_out3), .en(demultiplexer_2_out3), .clk(Clock_Signal), .Q(v1_q));  // open: clr
  Register #(.width(32)) a0 (
    .D(demultiplexer_1_out4), .en(demultiplexer_2_out4), .clk(Clock_Signal), .Q(a0_q));  // open: clr
  Register #(.width(32)) a1 (
    .D(demultiplexer_1_out5), .en(demultiplexer_2_out5), .clk(Clock_Signal), .Q(a1_q));  // open: clr
  Register #(.width(32)) a2 (
    .D(demultiplexer_1_out6), .en(demultiplexer_2_out6), .clk(Clock_Signal), .Q(a2_q));  // open: clr
  Register #(.width(32)) a3 (
    .D(demultiplexer_1_out7), .en(demultiplexer_2_out7), .clk(Clock_Signal), .Q(a3_q));  // open: clr
  Register #(.width(32)) t0 (.D(load_t0_write), .en(load_t0_enable), .clk(Clock_Signal), .Q(t0_q));  // open: clr
  Register #(.width(32)) t1 (.D(load_t1_write), .en(load_t1_enable), .clk(Clock_Signal), .Q(t1_q));  // open: clr
  Register #(.width(32)) t2 (.D(load_t2_write), .en(load_t2_enable), .clk(Clock_Signal), .Q(t2_q));  // open: clr
  Register #(.width(32)) t3 (.D(load_t3_write), .en(load_t3_enable), .clk(Clock_Signal), .Q(t3_q));  // open: clr
  Register #(.width(32)) t4 (.D(load_t4_write), .en(load_t4_enable), .clk(Clock_Signal), .Q(t4_q));  // open: clr
  Register #(.width(32)) t5 (.D(load_t5_write), .en(load_t5_enable), .clk(Clock_Signal), .Q(t5_q));  // open: clr
  Register #(.width(32)) t6 (.D(load_t6_write), .en(load_t6_enable), .clk(Clock_Signal), .Q(t6_q));  // open: clr
  Register #(.width(32)) t7 (.D(load_t7_write), .en(load_t7_enable), .clk(Clock_Signal), .Q(t7_q));  // open: clr
  Register #(.width(32)) s0 (
    .D(demultiplexer_1_out16), .en(demultiplexer_2_out16), .clk(Clock_Signal), .Q(s0_q));  // open: clr
  Register #(.width(32)) s1 (
    .D(demultiplexer_1_out17), .en(demultiplexer_2_out17), .clk(Clock_Signal), .Q(s1_q));  // open: clr
  Register #(.width(32)) s2 (
    .D(demultiplexer_1_out18), .en(demultiplexer_2_out18), .clk(Clock_Signal), .Q(s2_q));  // open: clr
  Register #(.width(32)) s3 (
    .D(demultiplexer_1_out19), .en(demultiplexer_2_out19), .clk(Clock_Signal), .Q(s3_q));  // open: clr
  Register #(.width(32)) s4 (
    .D(demultiplexer_1_out20), .en(demultiplexer_2_out20), .clk(Clock_Signal), .Q(s4_q));  // open: clr
  Register #(.width(32)) s5 (
    .D(demultiplexer_1_out21), .en(demultiplexer_2_out21), .clk(Clock_Signal), .Q(s5_q));  // open: clr
  Register #(.width(32)) s6 (
    .D(demultiplexer_1_out22), .en(demultiplexer_2_out22), .clk(Clock_Signal), .Q(s6_q));  // open: clr
  Register #(.width(32)) s7 (
    .D(demultiplexer_1_out23), .en(demultiplexer_2_out23), .clk(Clock_Signal), .Q(s7_q));  // open: clr
  Register #(.width(32)) t8 (
    .D(demultiplexer_1_out24), .en(demultiplexer_2_out24), .clk(Clock_Signal), .Q(t8_q));  // open: clr
  Register #(.width(32)) t9 (
    .D(demultiplexer_1_out25), .en(demultiplexer_2_out25), .clk(Clock_Signal), .Q(t9_q));  // open: clr
  Register #(.width(32)) k0 (
    .D(demultiplexer_1_out26), .en(demultiplexer_2_out26), .clk(Clock_Signal), .Q(k0_q));  // open: clr
  Register #(.width(32)) k1 (
    .D(demultiplexer_1_out27), .en(demultiplexer_2_out27), .clk(Clock_Signal), .Q(k1_q));  // open: clr
  Register #(.width(32)) gp (
    .D(demultiplexer_1_out28), .en(demultiplexer_2_out28), .clk(Clock_Signal), .Q(gp_q));  // open: clr
  Register #(.width(32)) sp (
    .D(demultiplexer_1_out29), .en(demultiplexer_2_out29), .clk(Clock_Signal), .Q(sp_q));  // open: clr
  Register #(.width(32)) fp (
    .D(demultiplexer_1_out30), .en(demultiplexer_2_out30), .clk(Clock_Signal), .Q(fp_q));  // open: clr
  Register #(.width(32)) ra (
    .D(demultiplexer_1_out31), .en(demultiplexer_2_out31), .clk(Clock_Signal), .Q(ra_q));  // open: clr
  Multiplexer #(.select(5), .width(32)) multiplexer_1 (
    .in0(zero_q), .in1(at_q), .in2(v0_q), .in3(v1_q), .in4(a0_q), .in5(a1_q), .in6(a2_q), .in7(a3_q),
    .in8(t0_q), .in9(t1_q), .in10(t2_q), .in11(t3_q), .in12(t4_q), .in13(t5_q), .in14(t6_q), .in15(t7_q),
    .in16(s0_q), .in17(s1_q), .in18(s2_q), .in19(s3_q), .in20(s4_q), .in21(s5_q), .in22(s6_q), .in23(s7_q),
    .in24(t8_q), .in25(t9_q), .in26(k0_q), .in27(k1_q), .in28(gp_q), .in29(sp_q), .in30(fp_q), .in31(ra_q),
    .out(Read_Register_1), .sel(RS_IN));
  Multiplexer #(.select(5), .width(32)) multiplexer_2 (
    .in0(zero_q), .in1(at_q), .in2(v0_q), .in3(v1_q), .in4(a0_q), .in5(a1_q), .in6(a2_q), .in7(a3_q),
    .in8(t0_q), .in9(t1_q), .in10(t2_q), .in11(t3_q), .in12(t4_q), .in13(t5_q), .in14(t6_q), .in15(t7_q),
    .in16(s0_q), .in17(s1_q), .in18(s2_q), .in19(s3_q), .in20(s4_q), .in21(s5_q), .in22(s6_q), .in23(s7_q),
    .in24(t8_q), .in25(t9_q), .in26(k0_q), .in27(k1_q), .in28(gp_q), .in29(sp_q), .in30(fp_q), .in31(ra_q),
    .out(Read_Register_2), .sel(RT_IN));
endmodule

module load (
  input  [31:0] ALU,
  input  [31:0] Load_IN,
  input  Slection_Bit,
  input  RegWrite,
  output [31:0] Write,
  output Enable
);

  Multiplexer #(.width(32)) multiplexer_1 (.in0(ALU), .in1(Load_IN), .out(Write), .sel(Slection_Bit));
  xor xor_1 (Enable, Slection_Bit, RegWrite);
endmodule
